// Logisim project HW2_KEGLEY.circ as structural Verilog: 4 circuits, main circuit main
module main (
  input  [3:0] A,
  input  [3:0] B,
  output [3:0] Q,
  output Overflow
);

  wire full_adder_1_carry_out, full_adder_2_carry_out, half_adder_1_carry;

  Half_adder half_adder_1 (.A(A[0]), .B(B[0]), .Sum(Q[0]), .Carry(half_adder_1_carry));
  Full_adder full_adder_1 (
    .A(A[1]), .B(B[1]), .Carry_in(half_adder_1_carry), .Sum(Q[1]), .Carry_out(full_adder_1_carry_out));
  Full_adder full_adder_2 (
    .A(A[2]), .B(B[2]), .Carry_in(full_adder_1_carry_out), .Sum(Q[2]), .Carry_out(full_adder_2_carry_out));
  Full_adder full_adder_3 (.A(A[3]), .B(B[3]), .Carry_in(full_adder_2_carry_out), .Sum(Q[3]), .Carry_out(Overflow));
endmodule

module XOR_tutorial (
  input  A,
  input  B,
  output Q
);

  wire and_1_out, and_2_out, not_1_out, not_2_out;

  not not_1 (not_1_out, B);
  not not_2 (not_2_out, A);
  and and_1 (and_1_out, A, not_1_out);
  and and_2 (and_2_out, not_2_out, B);
  or or_1 (Q, and_1_out, and_2_out);
endmodule

module Half_adder (
  input  A,
  input  B,
  output Sum,
  output Carry
);

  and and_1 (Carry, A, B);
  XOR_tutorial xor_tutorial_1 (.A(A), .B(B), .Q(Sum));
endmodule

module Full_adder (
  input  A,
  input  B,
  input  Carry_in,
  output Sum,
  output Carry_out
);

  wire and_1_out, and_2_out, xor_tutorial_1_q;

  XOR_tutorial xor_tutorial_1 (.A(A), .B(B), .Q(xor_tutorial_1_q));
  and and_1 (and_1_out, A, B);
  and and_2 (and_2_out, xor_tutorial_1_q, Carry_in);
  XOR_tutorial xor_tutorial_2 (.A(xor_tutorial_1_q), .B(Carry_in), .Q(Sum));
  or or_1 (Carry_out, and_1_out, and_2_out);
endmodule
