// Logisim project HW2_Skeleton.circ as structural Verilog: 4 circuits, main circuit main
module main (
  input  [3:0] A,
  input  [3:0] B,
  output [3:0] Q,
  output Overflow
);
endmodule

module XOR_tutorial (
  input  A,
  input  B,
  output Q
);

  wire and_1_out, and_2_out, not_1_out, not_2_out;

  not not_1 (not_1_out, B);
  not not_2 (not_2_out, A);
  and and_1 (and_1_out, A, not_1_out);
  and and_2 (and_2_out, not_2_out, B);
  or or_1 (Q, and_1_out, and_2_out);
endmodule

module Half_adder (
  input  A,
  input  B,
  output Sum,
  output Carry
);
endmodule

module Full_adder (
  input  A,
  input  B,
  input  Carry_in,
  output Sum,
  output Carry_out
);
endmodule
