// Logisim project HW3_KEGLEY.circ as structural Verilog: 4 circuits, main circuit main
module main (
  input  [3:0] D,
  input  WE,
  input  [1:0] R_id_A,
  input  [1:0] W_id,
  input  [1:0] R_id_B,
  output [3:0] Q_A,
  output [3:0] Q_B
);

  wire clock_1_out, decoder_1_out0, decoder_1_out1, decoder_1_out2, decoder_1_out3;
  wire [3:0] R_00_q, R_01_q, R_10_q, R_11_q;

  Clock clock_1 (.out(clock_1_out));
  Decoder #(.select(2)) decoder_1 (
    .out0(decoder_1_out0), .out1(decoder_1_out1), .out2(decoder_1_out2), .out3(decoder_1_out3), .sel(W_id),
    .en(WE));
  DFF_Register R_00 (.D(D), .WE(decoder_1_out0), .Clk(clock_1_out), .Q(R_00_q));
  DFF_Register R_01 (.D(D), .WE(decoder_1_out1), .Clk(clock_1_out), .Q(R_01_q));
  DFF_Register R_10 (.D(D), .WE(decoder_1_out2), .Clk(clock_1_out), .Q(R_10_q));
  DFF_Register R_11 (.D(D), .WE(decoder_1_out3), .Clk(clock_1_out), .Q(R_11_q));
  Multiplexer #(.select(2), .width(4)) multiplexer_1 (
    .in0(R_00_q), .in1(R_01_q), .in2(R_10_q), .in3(R_11_q), .out(Q_A), .sel(R_id_A));
  Multiplexer #(.select(2), .width(4)) multiplexer_2 (
    .in0(R_00_q), .in1(R_01_q), .in2(R_10_q), .in3(R_11_q), .out(Q_B), .sel(R_id_B));
endmodule

module D_Latch (
  input  D,
  input  Clk,
  output Q
);

  wire and_1_out, and_2_out, nor_1_out, not_1_out;

  not not_1 (not_1_out, D);
  and and_1 (and_1_out, D, Clk);
  and and_2 (and_2_out, Clk, not_1_out);
  nor nor_1 (nor_1_out, and_1_out, Q);
  nor nor_2 (Q, nor_1_out, and_2_out);

  // Notes on the sheet:
  //   S
  //   R
  //   DO NOT MODIFY
endmodule

module D_Flip_Flop (
  input  D,
  input  WE,
  input  Clk,
  output Q
);

  wire d_latch_1_q, multiplexer_1_out, not_1_out;

  Multiplexer multiplexer_1 (.in0(Q), .in1(D), .out(multiplexer_1_out), .sel(WE));
  not not_1 (not_1_out, Clk);
  D_Latch d_latch_1 (.D(multiplexer_1_out), .Clk(not_1_out), .Q(d_latch_1_q));
  D_Latch d_latch_2 (.D(d_latch_1_q), .Clk(Clk), .Q(Q));
endmodule

module DFF_Register (
  input  [3:0] D,
  input  WE,
  input  Clk,
  output [3:0] Q
);

  D_Flip_Flop d_flip_flop_1 (.D(D[0]), .WE(WE), .Clk(Clk), .Q(Q[0]));
  D_Flip_Flop d_flip_flop_2 (.D(D[1]), .WE(WE), .Clk(Clk), .Q(Q[1]));
  D_Flip_Flop d_flip_flop_3 (.D(D[2]), .WE(WE), .Clk(Clk), .Q(Q[2]));
  D_Flip_Flop d_flip_flop_4 (.D(D[3]), .WE(WE), .Clk(Clk), .Q(Q[3]));
endmodule
