// Logisim project sequentialcircuits.circ as structural Verilog: 4 circuits, main circuit main
module main (
  input  [3:0] D,
  input  WE,
  input  [1:0] W_id,
  input  [1:0] R_id_A,
  input  [1:0] R_id_B,
  output [3:0] Q_A,
  output [3:0] Q_B
);

  Decoder #(.select(2)) decoder_1 ();  // open: out0, out1, out2, out3, sel, en
  Multiplexer #(.select(2), .width(4)) multiplexer_1 ();  // open: in0, in1, in2, in3, out, sel
  Multiplexer #(.select(2), .width(4)) multiplexer_2 ();  // open: in0, in1, in2, in3, out, sel
  Clock clock_1 ();  // open: out
  DFF_Register R_00 ();  // open: D, WE, Clk, Q
  DFF_Register R_01 ();  // open: D, WE, Clk, Q
  DFF_Register R_10 ();  // open: D, WE, Clk, Q
  DFF_Register R_11 ();  // open: D, WE, Clk, Q
endmodule

module D_Latch (
  input  D,
  input  Clk,
  output Q
);

  wire and_1_out, and_2_out, nor_1_out, not_1_out;

  not not_1 (not_1_out, D);
  and and_1 (and_1_out, D, Clk);
  and and_2 (and_2_out, Clk, not_1_out);
  nor nor_1 (nor_1_out, and_1_out, Q);
  nor nor_2 (Q, nor_1_out, and_2_out);

  // Notes on the sheet:
  //   S
  //   R
  //   DO NOT MODIFY
endmodule

module D_Flip_Flop (
  input  D,
  input  WE,
  input  Clk,
  output Q
);

  wire d_latch_1_q;

  Multiplexer multiplexer_1 ();  // open: in0, in1, out, sel
  D_Latch d_latch_1 (.Q(d_latch_1_q));  // open: D, Clk
  D_Latch d_latch_2 ();  // open: D, Clk, Q
endmodule

module DFF_Register (
  input  [3:0] D,
  input  WE,
  input  Clk,
  output [3:0] Q
);

  D_Flip_Flop d_flip_flop_1 ();  // open: D, WE, Clk, Q
  D_Flip_Flop d_flip_flop_2 ();  // open: D, WE, Clk, Q
  D_Flip_Flop d_flip_flop_3 ();  // open: D, WE, Clk, Q
  D_Flip_Flop d_flip_flop_4 ();  // open: D, WE, Clk, Q
endmodule
