// Logisim project arithmeticcircuits.circ as structural Verilog: 15 circuits, main circuit Half_adder
module Half_adder (
  input  A,
  input  B,
  output Sum,
  output Carry
);

  Adder #(.width(1)) adder_1 (.a(A), .b(B), .out(Sum), .cout(Carry));  // open: cin
endmodule

module Full_Adder (
  input  Carry_in,
  input  A,
  input  B,
  output Sum,
  output Carry
);

  Adder #(.width(1)) adder_1 (.a(A), .b(B), .out(Sum), .cin(Carry_in), .cout(Carry));
endmodule

module DecoderExample1 (
  input  A,
  input  B,
  input  [1:0] S,
  output [3:0] Q
);

  wire componenta_1_q, componentb_1_q, componentc_1_q, componentd_1_q, decoder_1_out0, decoder_1_out1,
       decoder_1_out2, decoder_1_out3;

  Decoder #(.enable("false"), .select(2)) decoder_1 (
    .out0(decoder_1_out0), .out1(decoder_1_out1), .out2(decoder_1_out2), .out3(decoder_1_out3), .sel(S));
  ComponentA componenta_1 (.A(A), .B(B), .Q(componenta_1_q));
  ComponentB componentb_1 (.A(A), .B(B), .Q(componentb_1_q));
  ComponentC componentc_1 (.A(A), .B(B), .Q(componentc_1_q));
  ComponentD componentd_1 (.A(A), .B(B), .Q(componentd_1_q));
  and and_1 (Q[0], componenta_1_q, decoder_1_out0);
  and and_2 (Q[1], componentb_1_q, decoder_1_out1);
  and and_3 (Q[2], componentc_1_q, decoder_1_out2);
  and and_4 (Q[3], componentd_1_q, decoder_1_out3);
endmodule

module DecoderExample2 (
  input  A,
  input  B,
  input  [1:0] S,
  output [3:0] Q
);

  wire decoder_1_out0, decoder_1_out1, decoder_1_out2, decoder_1_out3;

  Decoder #(.enable("false"), .select(2)) decoder_1 (
    .out0(decoder_1_out0), .out1(decoder_1_out1), .out2(decoder_1_out2), .out3(decoder_1_out3), .sel(S));
  ComponentE componente_1 (.A(A), .B(B), .Enable(decoder_1_out0), .Q(Q[0]));
  ComponentF componentf_1 (.A(A), .B(B), .Enable(decoder_1_out1), .Q(Q[1]));
  ComponentG componentg_1 (.A(A), .B(B), .Enable(decoder_1_out2), .Q(Q[2]));
  ComponentH componenth_1 (.A(A), .B(B), .Enable(decoder_1_out3), .Q(Q[3]));
endmodule

module MultiplexorExample (
  input  A,
  input  B,
  input  [1:0] S,
  output Q
);

  wire componenta_1_q, componentb_1_q, componentc_1_q, componentd_1_q;

  ComponentA componenta_1 (.A(A), .B(B), .Q(componenta_1_q));
  ComponentB componentb_1 (.A(A), .B(B), .Q(componentb_1_q));
  ComponentC componentc_1 (.A(A), .B(B), .Q(componentc_1_q));
  ComponentD componentd_1 (.A(A), .B(B), .Q(componentd_1_q));
  Multiplexer #(.select(2)) multiplexer_1 (
    .in0(componenta_1_q), .in1(componentb_1_q), .in2(componentc_1_q), .in3(componentd_1_q), .out(Q), .sel(S));
endmodule

module TwoBitMultiplier (
  input  [1:0] A,
  input  [1:0] B,
  output [3:0] P
);

  wire A0B1_out, A1B0_out, A1B1_out, half_adder_1_carry;

  and A0B0 (P[0], A[0], B[0]);
  and A0B1 (A0B1_out, A[0], B[1]);
  and A1B0 (A1B0_out, A[1], B[0]);
  and A1B1 (A1B1_out, A[1], B[1]);
  Half_adder half_adder_1 (.A(A0B1_out), .B(A1B0_out), .Sum(P[1]), .Carry(half_adder_1_carry));
  Half_adder half_adder_2 (.A(half_adder_1_carry), .B(A1B1_out), .Sum(P[2]), .Carry(P[3]));
endmodule

module ThreeBitMultiplier (
  input  [2:0] A,
  input  [2:0] B,
  output [5:0] P
);

  wire A0B1_out, A0B2_out, A1B0_out, A1B1_out, A1B2_out, A2B0_out, A2B1_out, A2B2_out, full_adder_1_carry,
       full_adder_1_sum, full_adder_2_carry, full_adder_2_sum, half_adder_1_carry, half_adder_2_carry,
       half_adder_3_carry;

  and A0B0 (P[0], A[0], B[0]);
  and A0B1 (A0B1_out, A[0], B[1]);
  and A1B0 (A1B0_out, A[1], B[0]);
  and A1B1 (A1B1_out, A[1], B[1]);
  and A2B0 (A2B0_out, A[2], B[0]);
  and A0B2 (A0B2_out, A[0], B[2]);
  and A2B1 (A2B1_out, A[2], B[1]);
  and A1B2 (A1B2_out, A[1], B[2]);
  and A2B2 (A2B2_out, A[2], B[2]);
  Half_adder half_adder_1 (.A(A0B1_out), .B(A1B0_out), .Sum(P[1]), .Carry(half_adder_1_carry));
  Full_Adder full_adder_1 (
    .Carry_in(half_adder_1_carry), .A(A1B1_out), .B(A2B0_out), .Sum(full_adder_1_sum),
    .Carry(full_adder_1_carry));
  Half_adder half_adder_2 (.A(full_adder_1_sum), .B(A0B2_out), .Sum(P[2]), .Carry(half_adder_2_carry));
  Full_Adder full_adder_2 (
    .Carry_in(half_adder_2_carry), .A(full_adder_1_carry), .B(A2B1_out), .Sum(full_adder_2_sum),
    .Carry(full_adder_2_carry));
  Half_adder half_adder_3 (.A(full_adder_2_sum), .B(A1B2_out), .Sum(P[3]), .Carry(half_adder_3_carry));
  Full_Adder full_adder_3 (
    .Carry_in(half_adder_3_carry), .A(full_adder_2_carry), .B(A2B2_out), .Sum(P[4]), .Carry(P[5]));
endmodule

module ComponentA (
  input  A,
  input  B,
  output Q
);

  xor xor_1 (Q, A, B);
endmodule

module ComponentB (
  input  A,
  input  B,
  output Q
);

  and and_1 (Q, A, B);
endmodule

module ComponentC (
  input  A,
  input  B,
  output Q
);

  nor nor_1 (Q, A, B);
endmodule

module ComponentD (
  input  A,
  input  B,
  output Q
);

  or or_1 (Q, A, B);
endmodule

module ComponentE (
  input  A,
  input  B,
  input  Enable,
  output Q
);

  wire xor_1_out;

  xor xor_1 (xor_1_out, A, B);
  and and_1 (Q, xor_1_out, Enable);
endmodule

module ComponentF (
  input  A,
  input  B,
  input  Enable,
  output Q
);

  wire and_1_out;

  and and_1 (and_1_out, A, B);
  and and_2 (Q, and_1_out, Enable);
endmodule

module ComponentG (
  input  A,
  input  B,
  input  Enable,
  output Q
);

  wire nor_1_out;

  nor nor_1 (nor_1_out, A, B);
  and and_1 (Q, nor_1_out, Enable);
endmodule

module ComponentH (
  input  A,
  input  B,
  input  Enable,
  output Q
);

  wire or_1_out;

  or or_1 (or_1_out, A, B);
  and and_1 (Q, or_1_out, Enable);
endmodule
