// Logisim project Project1_Skeleton.circ as structural Verilog: 11 circuits, main circuit main
module main (
  input  [3:0] A,
  input  [3:0] B,
  input  [2:0] Opcode,
  output [3:0] Q
);

  wire [3:0] undriven;

  Addition addition_1 (.A(A), .B(B), .Q(Q));
  Multiplexer #(.select(3), .width(4)) multiplexer_1 (
    .in0(undriven), .out(Q));  // open: in1, in2, in3, in4, in5, in6, in7, sel
endmodule

module Half_Adder (
  input  A,
  input  B,
  output Sum,
  output Carry
);

  Adder #(.width(1)) adder_1 (.a(A), .b(B), .out(Sum), .cout(Carry));  // open: cin
endmodule

module Full_Adder (
  input  A,
  input  B,
  input  Cin,
  output Sum,
  output Carry
);

  Adder #(.width(1)) adder_1 (.a(A), .b(B), .out(Sum), .cin(Cin), .cout(Carry));
endmodule

module No_Operation (
  input  [3:0] A,
  input  [3:0] B,
  output [3:0] Q
);

  // NoConnect on A

  assign Q = B;
endmodule

module Equality_Comparison (
  input  [3:0] A,
  input  [3:0] B,
  output [3:0] Q
);

  wire and_1_out, and_2_out, not_1_out, not_2_out, not_3_out, not_4_out, xor_1_out, xor_2_out, xor_3_out,
       xor_4_out;

  xor xor_1 (xor_1_out, A[0], B[0]);
  not not_1 (not_1_out, xor_1_out);
  xor xor_2 (xor_2_out, A[1], B[1]);
  not not_2 (not_2_out, xor_2_out);
  xor xor_3 (xor_3_out, A[2], B[2]);
  not not_3 (not_3_out, xor_3_out);
  xor xor_4 (xor_4_out, A[3], B[3]);
  not not_4 (not_4_out, xor_4_out);
  and and_1 (and_1_out, not_1_out, not_2_out);
  and and_2 (and_2_out, not_3_out, not_4_out);
  and and_3 (Q[0], and_1_out, and_2_out);

  assign Q[3:1] = 3'b000;
endmodule

module Bitwise_XOR (
  input  [3:0] A,
  input  [3:0] B,
  output [3:0] Q
);

  xor xor_1 (Q[0], A[0], B[0]);
  xor xor_2 (Q[1], A[1], B[1]);
  xor xor_3 (Q[2], A[2], B[2]);
  xor xor_4 (Q[3], A[3], B[3]);
endmodule

module Inverter (
  input  [3:0] A,
  input  [3:0] B,
  output [3:0] Q
);

  // NoConnect on A
  not not_1 (Q[0], B[0]);
  not not_2 (Q[1], B[1]);
  not not_3 (Q[2], B[2]);
  not not_4 (Q[3], B[3]);
endmodule

module Increment (
  input  [3:0] A,
  input  [3:0] B,
  output [3:0] Q
);

  wire half_adder_1_carry, half_adder_2_carry, half_adder_3_carry;

  // NoConnect on A
  Half_Adder half_adder_1 (.A(1'b1), .B(B[0]), .Sum(Q[0]), .Carry(half_adder_1_carry));
  Half_Adder half_adder_2 (.A(half_adder_1_carry), .B(B[1]), .Sum(Q[1]), .Carry(half_adder_2_carry));
  Half_Adder half_adder_3 (.A(half_adder_2_carry), .B(B[2]), .Sum(Q[2]), .Carry(half_adder_3_carry));
  Half_Adder half_adder_4 (.A(half_adder_3_carry), .B(B[3]), .Sum(Q[3]));  // open: Carry
endmodule

module Addition (
  input  [3:0] A,
  input  [3:0] B,
  output [3:0] Q
);

  Adder #(.width(4)) adder_1 (.a(A), .b(B), .out(Q));  // open: cin, cout
endmodule

module Subtraction (
  input  [3:0] A,
  input  [3:0] B,
  output [3:0] Q
);

  wire [3:0] increment_1_q, inverter_1_q;

  Inverter inverter_1 (.B(B), .Q(inverter_1_q));  // open: A
  Increment increment_1 (.B(inverter_1_q), .Q(increment_1_q));  // open: A
  Addition addition_1 (.A(A), .B(increment_1_q), .Q(Q));
endmodule

module Multiplication (
  input  [3:0] A,
  input  [3:0] B,
  output [3:0] Q
);

  // AND_Gate and_1 is placed but not wired
endmodule
