// Logisim project Project2_Skeleton.circ as structural Verilog: 7 circuits, main circuit Multi_Purpose_Processor
module Incrementor (
  input  [3:0] A,
  output [3:0] Q
);

  Adder #(.width(4)) adder_1 (.a(A), .b(4'b0001), .out(Q));  // open: cin, cout
endmodule

module Arithmetic_Logic_Unit (
  input  [3:0] A,
  input  [3:0] B,
  input  [2:0] Opcode,
  output [3:0] Q,
  output Z_flag
);

  wire [0:0] comparator_1_eq;
  wire [3:0] adder_1_out, incrementor_1_q, multiplier_1_out, not_1_out, subtractor_1_out, xor_1_out;

  assign not_1_out = ~A;  // NOT_Gate not_1, 4 bits wide
  Comparator #(.width(4)) comparator_1 (.a(A), .b(B), .eq(comparator_1_eq[0]));  // open: gt, lt
  assign xor_1_out = A ^ B;  // XOR_Gate xor_1, 4 bits wide
  Adder #(.width(4)) adder_1 (.a(A), .b(B), .out(adder_1_out));  // open: cin, cout
  Subtractor #(.width(4)) subtractor_1 (.a(A), .b(B), .out(subtractor_1_out));  // open: bin, bout
  Multiplier #(.width(4)) multiplier_1 (.a(A), .b(B), .out(multiplier_1_out));  // open: cin, cout
  Incrementor incrementor_1 (.A(A), .Q(incrementor_1_q));
  Multiplexer #(.select(3), .width(4)) multiplexer_1 (
    .in0(B), .in1({3'b000, comparator_1_eq[0]}), .in2(xor_1_out), .in3(not_1_out), .in4(incrementor_1_q),
    .in5(adder_1_out), .in6(subtractor_1_out), .in7(multiplier_1_out), .out(Q), .sel(Opcode));
  nor nor_1 (Z_flag, Q[0], Q[1], Q[2], Q[3]);
endmodule

module Register_File (
  input  [3:0] D,
  input  WE,
  input  [1:0] W_id,
  input  [1:0] R_id_A,
  input  [1:0] R_id_B,
  input  Clk,
  input  Reset,
  output [3:0] Q_A,
  output [3:0] Q_B
);

  wire decoder_1_out0, decoder_1_out1, decoder_1_out2, decoder_1_out3;
  wire [3:0] R_00_q, R_01_q, R_10_q, R_11_q;

  Decoder #(.select(2)) decoder_1 (
    .out0(decoder_1_out0), .out1(decoder_1_out1), .out2(decoder_1_out2), .out3(decoder_1_out3), .sel(W_id),
    .en(WE));
  Register #(.width(4)) R_00 (.D(D), .en(decoder_1_out0), .clk(Clk), .Q(R_00_q), .clr(Reset));
  Register #(.width(4)) R_01 (.D(D), .en(decoder_1_out1), .clk(Clk), .Q(R_01_q), .clr(Reset));
  Register #(.width(4)) R_10 (.D(D), .en(decoder_1_out2), .clk(Clk), .Q(R_10_q), .clr(Reset));
  Register #(.width(4)) R_11 (.D(D), .en(decoder_1_out3), .clk(Clk), .Q(R_11_q), .clr(Reset));
  Multiplexer #(.select(2), .width(4)) multiplexer_1 (
    .in0(R_00_q), .in1(R_01_q), .in2(R_10_q), .in3(R_11_q), .out(Q_A), .sel(R_id_A));
  Multiplexer #(.select(2), .width(4)) multiplexer_2 (
    .in0(R_00_q), .in1(R_01_q), .in2(R_10_q), .in3(R_11_q), .out(Q_B), .sel(R_id_B));
endmodule

module Flag_Register (
  input  Z_in,
  input  WE,
  input  Clk,
  input  Reset,
  output Z_flag
);

  wire d_ff_1_qn, multiplexer_1_out;

  D_Flip_Flop d_ff_1 (.D(multiplexer_1_out), .clk(Clk), .Q(Z_flag), .Qn(d_ff_1_qn), .reset(Reset));  // open: preset
  Multiplexer multiplexer_1 (.in0(Z_flag), .in1(Z_in), .out(multiplexer_1_out), .sel(WE));
  // NoConnect on d_ff_1_qn
endmodule

module PC_Register (
  input  [3:0] Jump_Addr,
  input  Do_Jump,
  input  Clk,
  input  Reset,
  output [3:0] M_addr
);

  wire [3:0] incrementor_1_q, multiplexer_1_out;

  Incrementor incrementor_1 (.A(M_addr), .Q(incrementor_1_q));
  Register #(.width(4)) register_1 (.D(multiplexer_1_out), .en(1'b1), .clk(Clk), .Q(M_addr), .clr(Reset));
  Multiplexer #(.width(4)) multiplexer_1 (
    .in0(incrementor_1_q), .in1(Jump_Addr), .out(multiplexer_1_out), .sel(Do_Jump));
endmodule

module Control_Unit (
  input  [8:0] M,
  input  Z_flag,
  output WE,
  output [1:0] W_id,
  output [1:0] R_id_A,
  output [1:0] R_id_B,
  output [2:0] Opcode,
  output Operand,
  output Do_Jump,
  output [3:0] Jump_Addr
);

  wire and_1_out, and_2_out, and_3_out, and_4_out, not_1_out, not_2_out, not_3_out, not_4_out, not_5_out,
       not_6_out, or_1_out;

  not not_1 (not_1_out, Z_flag);
  not not_2 (not_2_out, M[6]);
  not not_3 (not_3_out, M[4]);
  not not_4 (not_4_out, M[5]);
  not not_5 (not_5_out, M[5]);
  not not_6 (not_6_out, M[4]);
  and and_1 (and_1_out, M[8], not_2_out);
  and and_2 (and_2_out, not_3_out, not_4_out, Z_flag);
  and and_3 (and_3_out, M[4], not_5_out, not_1_out);
  and and_4 (and_4_out, not_6_out, M[5]);
  or or_1 (or_1_out, and_2_out, and_3_out, and_4_out);
  and and_5 (Do_Jump, and_1_out, or_1_out);
  not not_7 (WE, Do_Jump);

  assign Jump_Addr = M[3:0];
  assign Opcode = M[6:4];
  assign Operand = M[7];
  assign R_id_A = M[3:2];
  assign R_id_B = M[1:0];
  assign W_id = M[3:2];
endmodule

module Multi_Purpose_Processor (
  input  [3:0] I,
  input  Reset,
  output [3:0] Q_A,
  output [3:0] Q_B
);

  wire arithmetic_logic_unit_1_z_flag, clock_1_out, control_unit_1_do_jump, control_unit_1_operand,
       control_unit_1_we, flag_register_1_z_flag;
  wire [1:0] control_unit_1_r_id_a, control_unit_1_r_id_b, control_unit_1_w_id;
  wire [2:0] control_unit_1_opcode;
  wire [3:0] arithmetic_logic_unit_1_q, control_unit_1_jump_addr, multiplexer_1_out, pc_register_1_m_addr;
  wire [8:0] rom_1_data;

  ROM #(.addrWidth(4), .dataWidth(9)) rom_1 (.addr(pc_register_1_m_addr), .data(rom_1_data));
  Clock clock_1 (.out(clock_1_out));
  Multiplexer #(.width(4)) multiplexer_1 (.in0(Q_B), .in1(I), .out(multiplexer_1_out), .sel(control_unit_1_operand));
  Control_Unit control_unit_1 (
    .M(rom_1_data), .Z_flag(flag_register_1_z_flag), .WE(control_unit_1_we), .W_id(control_unit_1_w_id),
    .R_id_A(control_unit_1_r_id_a), .R_id_B(control_unit_1_r_id_b), .Opcode(control_unit_1_opcode),
    .Operand(control_unit_1_operand), .Do_Jump(control_unit_1_do_jump), .Jump_Addr(control_unit_1_jump_addr));
  Arithmetic_Logic_Unit arithmetic_logic_unit_1 (
    .A(Q_A), .B(multiplexer_1_out), .Opcode(control_unit_1_opcode), .Q(arithmetic_logic_unit_1_q),
    .Z_flag(arithmetic_logic_unit_1_z_flag));
  PC_Register pc_register_1 (
    .Jump_Addr(control_unit_1_jump_addr), .Do_Jump(control_unit_1_do_jump), .Clk(clock_1_out), .Reset(Reset),
    .M_addr(pc_register_1_m_addr));
  Flag_Register flag_register_1 (
    .Z_in(arithmetic_logic_unit_1_z_flag), .WE(control_unit_1_we), .Clk(clock_1_out), .Reset(Reset),
    .Z_flag(flag_register_1_z_flag));
  Register_File register_file_1 (
    .D(arithmetic_logic_unit_1_q), .WE(control_unit_1_we), .W_id(control_unit_1_w_id),
    .R_id_A(control_unit_1_r_id_a), .R_id_B(control_unit_1_r_id_b), .Clk(clock_1_out), .Reset(Reset),
    .Q_A(Q_A), .Q_B(Q_B));

  // Notes on the sheet:
  //   contents of rom_1 (hex, n*v repeats v):
  //   80 40 4 e4 116 88 126
endmodule
