// Logisim project sequentialcircuits.circ as structural Verilog: 6 circuits, main circuit Feedback
module Feedback (
  input  A,
  output Q
);

  or or_1 (Q, A, Q);
endmodule

module SR_Latch (
  input  S,
  input  R,
  output Qnot,
  output Q
);

  nor nor_1 (Qnot, S, Q);
  nor nor_2 (Q, Qnot, R);
endmodule

module D_Flip_Flop_NAND (
  input  D,
  output Q,
  output Qnot
);

  wire Clk_out, nand_1_out, nand_2_out, not_1_out;

  Clock Clk (.out(Clk_out));
  not not_1 (not_1_out, D);
  nand nand_1 (nand_1_out, D, Clk_out);
  nand nand_2 (nand_2_out, not_1_out, Clk_out);
  nand nand_3 (Q, nand_1_out, Qnot);
  nand nand_4 (Qnot, Q, nand_2_out);
endmodule

module D_Latch (
  input  D,
  input  C,
  output Qnot,
  output Q
);

  wire and_1_out, and_2_out, not_1_out;

  not not_1 (not_1_out, D);
  and and_1 (and_1_out, D, C);
  and and_2 (and_2_out, C, not_1_out);
  nor nor_1 (Qnot, and_1_out, Q);
  nor nor_2 (Q, Qnot, and_2_out);

  // Notes on the sheet:
  //   S
  //   R
endmodule

module D_Flip_Flop (
  input  D,
  input  Clk,
  output Qnot,
  output Q
);

  wire d_latch_1_q, d_latch_1_qnot, not_1_out;

  not not_1 (not_1_out, Clk);
  // NoConnect on d_latch_1_qnot
  D_Latch d_latch_1 (.D(D), .C(not_1_out), .Qnot(d_latch_1_qnot), .Q(d_latch_1_q));
  D_Latch d_latch_2 (.D(d_latch_1_q), .C(Clk), .Qnot(Qnot), .Q(Q));
endmodule

module D_Flip_Flop_Register (
  input  A0,
  input  A1,
  input  A2,
  input  A3,
  input  C,
  output Q0,
  output Q1,
  output Q2,
  output Q3
);

  D_Flip_Flop d_flip_flop_1 (.D(A0), .Clk(C), .Q(Q0));  // open: Qnot
  D_Flip_Flop d_flip_flop_2 (.D(A1), .Clk(C), .Q(Q1));  // open: Qnot
  D_Flip_Flop d_flip_flop_3 (.D(A2), .Clk(C), .Q(Q2));  // open: Qnot
  D_Flip_Flop d_flip_flop_4 (.D(A3), .Clk(C), .Q(Q3));  // open: Qnot
endmodule
